# Fritzing sketch Runt Rover Wiring (saved by Fritzing 0.9.3b)

parts:
  M1 = DC Motor
  M2 = DC Motor
  Part2 = Tessel 2
  VCC1 = Battery block 9V
  S1 = H-Bridge with L298N

nets:
  N1: M1.pin_1, S1.OUT4-Motor2
  N2: M1.pin_2, S1.OUT3-Motor2
  N3: M2.pin_1, S1.OUT1-Motor1
  N4: M2.pin_2, S1.OUT2-Motor1
  GND: Part2.GND, VCC1.-, S1.GND
  3V3: Part2.3V3, S1.5V
  N5: Part2.5#35, S1.IN4
  N6: Part2.6#36, S1.IN3
  N7: Part2.5#75, S1.IN2
  N8: Part2.6#76, S1.IN1
  N9: VCC1.+, S1.12V

custom parts:
  Tessel 2: Draft version of Tessel 2
  H-Bridge with L298N: h-bridge
